# Fritzing sketch servo_rpi5 (saved by Fritzing 0.9.3b)

parts:
  A1 = Raspberry Pi 5
  J1 = Basic Servo
  IC1 = Rasberry Pi NIOR Camera [chip_label=IC package="DIP (Dual Inline) [THT]"]  # not connected

nets:
  5V: A1.5V, A1.Fan-5V, J1.vcc
  GND: A1.GND, J1.gnd
  N1: A1.GPIO4, J1.pulse

notes:
  NOIR Camera

custom parts:
  Raspberry Pi 5: The RPi5, a faster version of the awesome Raspberry Pi4B ARM Board with 40 pin gpio.
  Rasberry Pi NIOR Camera: Camera
